# Fritzing sketch lab (saved by Fritzing 0.9.9b)
breadboards: 1

parts:
  Arduino_Uno = Arduino Uno (Rev3) - ICSP
  LCD1 = LCD screen
  Resistor(Known) = Resistor [tolerance=±5% power=0.25 resistance=220 package=THT]
  Resistor(Unknown) = Resistor [tolerance=±5% power=0.25 resistance=220 package=THT]
  R2 = Resistor [tolerance=±5% power=0.25 resistance=100 package=THT]  # not connected
  R3 = Resistor [tolerance=±5% power=0.25 resistance=150 package=THT]  # not connected
  R4 = Resistor [tolerance=±5% power=0.25 resistance=330 package=THT]  # not connected
  R5 = Resistor [tolerance=±5% power=0.25 resistance=680 package=THT]  # not connected
  R6 = Resistor [tolerance=±5% power=0.25 resistance=1k package=THT]  # not connected
  R7 = Resistor [tolerance=±5% power=0.25 resistance=2.2k package=THT]  # not connected
  R1 = Resistor [tolerance=±5% power=0.25 resistance=220 package=THT]  # not connected

nets:
  N1: Arduino_Uno.A5/SCL, Resistor(Known).Pin_0, Resistor(Unknown).Pin_1
  5V: Arduino_Uno.5V, LCD1.VDD, LCD1.LED+, Resistor(Known).Pin_1
  GND: Arduino_Uno.GND, LCD1.VSS, LCD1.R/W, LCD1.LED-, Resistor(Unknown).Pin_0
  N2: Arduino_Uno.D11_PWM/MOSI, LCD1.E
  N3: Arduino_Uno.D12/MISO, LCD1.RS
  N4: Arduino_Uno.D2, LCD1.DB7
  N5: Arduino_Uno.D3_PWM, LCD1.DB6
  N6: Arduino_Uno.D4, LCD1.DB5
  N7: Arduino_Uno.D5_PWM, LCD1.DB4

notes:
  Resistors to be tested:
